// Logisim project 2 - AND using transistors.circ as structural Verilog: 1 circuit, main circuit main
module main (
  input  Input_A,
  input  Input_B,
  output Output
);

  wire transistor_4_out;

  Transistor transistor_1 (.in(1'b1), .out(Output), .gate(Input_A));
  Transistor transistor_2 (.in(1'b1), .out(Output), .gate(Input_B));
  Transistor #(.\type ("n")) transistor_3 (.in(transistor_4_out), .out(Output), .gate(Input_A));
  Transistor #(.\type ("n")) transistor_4 (.in(1'b0), .out(transistor_4_out), .gate(Input_B));
endmodule
