// Logisim project 3 - XNOR using NOR.circ as structural Verilog: 2 circuits, main circuit main
module main (
  input  A,
  input  A_2,
  input  A_3,
  input  A_4,
  input  A_5,
  input  B,
  input  B_2,
  input  B_3,
  input  B_4,
  input  B_5,
  input  X,
  input  Y,
  input  A_6,
  input  Z,
  input  A_7,
  input  X_2,
  input  Y_2,
  input  Z_2,
  output Q,
  output Q_2,
  output Q_3,
  output Q_4,
  output Q_5,
  output Q_6,
  output Q_7,
  output Q_8,
  output Q_9
);

  wire and_1_out, and_2_out, nor_2_out, nor_3_out, nor_4_out, nor_5_out, nor_6_out, nor_7_out, nor_9_out,
       nor_10_out, nor_11_out, not_1_out, not_2_out, not_5_out, not_6_out, or_2_out, or_3_out, or_5_out,
       or_6_out, or_7_out, or_8_out;

  not not_1 (not_1_out, A_2);
  not not_2 (not_2_out, B);
  nor nor_1 (Q_7, A_6, A_6);
  not not_3 (Q_8, A_7);
  nor nor_2 (nor_2_out, not_1_out, not_2_out);
  nor nor_3 (nor_3_out, A_2, B);
  nor nor_4 (nor_4_out, nor_2_out, nor_3_out);
  not not_4 (Q, nor_4_out);
  and and_1 (and_1_out, A_3, B_2);
  nor nor_5 (nor_5_out, A_3, B_2);
  or or_1 (Q_2, and_1_out, nor_5_out);
  and and_2 (and_2_out, X, Y);
  or or_2 (or_2_out, X_2, Z_2);
  or or_3 (or_3_out, Y_2, Z_2);
  or or_4 (Q_6, and_2_out, Z);
  and and_3 (Q_9, or_2_out, or_3_out);
  nor nor_6 (nor_6_out, A, B_3);
  or or_5 (or_5_out, A, nor_6_out);
  or or_6 (or_6_out, nor_6_out, B_3);
  and and_4 (Q_3, or_5_out, or_6_out);
  or or_7 (or_7_out, A_4, nor_7_out);
  nor nor_7 (nor_7_out, A_4, B_4);
  or or_8 (or_8_out, nor_7_out, B_4);
  not not_5 (not_5_out, or_7_out);
  not not_6 (not_6_out, or_8_out);
  nor nor_8 (Q_4, not_5_out, not_6_out);
  nor nor_9 (nor_9_out, A_5, B_5);
  nor nor_10 (nor_10_out, A_5, nor_9_out);
  nor nor_11 (nor_11_out, nor_9_out, B_5);
  nor nor_12 (Q_5, nor_10_out, nor_11_out);

  // Notes on the sheet:
  //   The simple approach using just NOR
  //   NOT A == A NOR A
  //   Intermediary steps
  //   (X AND Y) OR Z == (X OR Z) AND (Y OR Z)
  //   The common approach in real hardware
endmodule

module XOR (
  input  A,
  input  B,
  output Q
);

  wire nor_1_out, nor_2_out, nor_3_out, nor_4_out;

  nor nor_1 (nor_1_out, A, B);
  nor nor_2 (nor_2_out, A, nor_1_out);
  nor nor_3 (nor_3_out, nor_1_out, B);
  nor nor_4 (nor_4_out, nor_2_out, nor_3_out);
  nor nor_5 (Q, nor_4_out, nor_4_out);
endmodule
