// Logisim project 4 - Full Adder.circ as structural Verilog: 3 circuits, main circuit main
// Full adder
module main (
  input  Input_Carry,
  input  Input_A,
  input  Input_B,
  output Output_Carry,
  output Output_Sum
);

  wire nor_1_out, nor_2_out, nor_3_out, nor_4_out, nor_5_out, nor_6_out, nor_7_out;

  nor nor_1 (nor_1_out, Input_A, Input_B);
  nor nor_2 (nor_2_out, Input_A, nor_1_out);
  nor nor_3 (nor_3_out, nor_1_out, Input_B);
  nor nor_4 (nor_4_out, nor_2_out, nor_3_out);
  nor nor_5 (nor_5_out, Input_Carry, nor_4_out);
  nor nor_6 (nor_6_out, Input_Carry, nor_5_out);
  nor nor_7 (nor_7_out, nor_5_out, nor_4_out);
  nor nor_8 (Output_Carry, nor_1_out, nor_5_out);
  nor nor_9 (Output_Sum, nor_6_out, nor_7_out);
endmodule

module Carry_Out (
  input  A,
  input  B,
  output C
);

  wire not_1_out, not_2_out;

  not not_1 (not_1_out, A);
  not not_2 (not_2_out, B);
  nor nor_1 (C, not_1_out, not_2_out);
endmodule

module Half_adder (
  input  A,
  input  B,
  input  A_2,
  input  B_2,
  output C,
  output Q,
  output C_2,
  output Q_2
);

  wire nor_2_out, nor_3_out, nor_4_out, nor_6_out, nor_7_out, nor_8_out, nor_9_out, not_1_out, not_2_out,
       not_3_out, not_4_out;

  not not_1 (not_1_out, A_2);
  not not_2 (not_2_out, B_2);
  nor nor_1 (C_2, not_1_out, not_2_out);
  not not_3 (not_3_out, A);
  not not_4 (not_4_out, B);
  nor nor_2 (nor_2_out, A, B);
  nor nor_3 (nor_3_out, not_1_out, C_2);
  nor nor_4 (nor_4_out, C_2, not_2_out);
  nor nor_5 (C, not_3_out, not_4_out);
  nor nor_6 (nor_6_out, A, nor_2_out);
  nor nor_7 (nor_7_out, nor_2_out, B);
  nor nor_8 (nor_8_out, nor_3_out, nor_4_out);
  nor nor_9 (nor_9_out, nor_6_out, nor_7_out);
  not not_5 (Q_2, nor_8_out);
  not not_6 (Q, nor_9_out);
endmodule
