// Logisim project 5 - 8-bit Adder.circ as structural Verilog: 1 circuit, main circuit main
module main (
  input  [7:0] A,
  input  CIn,
  input  [7:0] B,
  output [7:0] Out,
  output COut
);

  wire main_1_output_carry, main_2_output_carry, main_3_output_carry, main_4_output_carry,
       main_5_output_carry, main_6_output_carry, main_7_output_carry;

  _4___Full_Adder_main main_1 (
    .Input_Carry(CIn), .Input_A(A[0]), .Input_B(B[0]), .Output_Carry(main_1_output_carry), .Output_Sum(Out[0]));
  _4___Full_Adder_main main_2 (
    .Input_Carry(main_1_output_carry), .Input_A(A[1]), .Input_B(B[1]), .Output_Carry(main_2_output_carry),
    .Output_Sum(Out[1]));
  _4___Full_Adder_main main_3 (
    .Input_Carry(main_2_output_carry), .Input_A(A[2]), .Input_B(B[2]), .Output_Carry(main_3_output_carry),
    .Output_Sum(Out[2]));
  _4___Full_Adder_main main_4 (
    .Input_Carry(main_3_output_carry), .Input_A(A[3]), .Input_B(B[3]), .Output_Carry(main_4_output_carry),
    .Output_Sum(Out[3]));
  _4___Full_Adder_main main_5 (
    .Input_Carry(main_4_output_carry), .Input_A(A[4]), .Input_B(B[4]), .Output_Carry(main_5_output_carry),
    .Output_Sum(Out[4]));
  _4___Full_Adder_main main_6 (
    .Input_Carry(main_5_output_carry), .Input_A(A[5]), .Input_B(B[5]), .Output_Carry(main_6_output_carry),
    .Output_Sum(Out[5]));
  _4___Full_Adder_main main_7 (
    .Input_Carry(main_6_output_carry), .Input_A(A[6]), .Input_B(B[6]), .Output_Carry(main_7_output_carry),
    .Output_Sum(Out[6]));
  _4___Full_Adder_main main_8 (
    .Input_Carry(main_7_output_carry), .Input_A(A[7]), .Input_B(B[7]), .Output_Carry(COut),
    .Output_Sum(Out[7]));
endmodule
