// Logisim project 6 - 8-bit add-sub.circ as structural Verilog: 2 circuits, main circuit main
module main (
  input  [7:0] A,
  input  Sub,
  input  [7:0] B,
  output [7:0] Q,
  output C_Out
);

  wire Mode_ctrl_carry_out;
  wire [7:0] Mode_ctrl_out;

  Subtract_Control Mode_ctrl (.In(B), .Carry_out(Mode_ctrl_carry_out), .Out(Mode_ctrl_out), .Subtract(Sub));
  _5___8_bit_Adder_main _8_bit_Full_Adder (.A(A), .Out(Q), .CIn(Mode_ctrl_carry_out), .B(Mode_ctrl_out), .COut(C_Out));
endmodule

module Subtract_Control (
  input  Subtract,
  input  [7:0] In,
  output Carry_out,
  output [7:0] Out
);

  wire [7:7] not_1_out;

  not not_1 (not_1_out[7], Subtract);
  assign Out = ~(In ^ {8{not_1_out[7]}});  // XNOR_Gate xnor_1, 8 bits wide

  assign Carry_out = Subtract;
endmodule
