// Logisim project 0 - AND using NOR gates.circ as structural Verilog: 1 circuit, main circuit main
module main (
  input  A,
  input  B,
  output Q
);

  wire not_1_out, not_2_out;

  not not_1 (not_1_out, A);
  not not_2 (not_2_out, B);
  nor nor_1 (Q, not_1_out, not_2_out);
endmodule
