// Logisim project 1 - SR Latch using NOR gates.circ as structural Verilog: 1 circuit, main circuit main
module main (
  input  Reset,
  input  Set,
  output Q,
  output Q_prime
);

  nor nor_1 (Q, Reset, Q_prime);
  nor nor_2 (Q_prime, Q, Set);
endmodule
