// Logisim project 2 - Clocked SR latch.circ as structural Verilog: 1 circuit, main circuit main
module main (
  input  R,
  input  Clk,
  input  S,
  output Q,
  output Q_prime
);

  wire and_1_out, and_2_out;

  and and_1 (and_1_out, R, Clk);
  and and_2 (and_2_out, Clk, S);
  _1___SR_Latch_using_NOR_gates_main Latch (.Reset(and_1_out), .Set(and_2_out), .Q(Q), .Q_prime(Q_prime));
endmodule
