// Logisim project 3 - D latch.circ as structural Verilog: 4 circuits, main circuit main
module main (
  input  Clk,
  input  D,
  output Q,
  output Q_prime
);

  wire not_1_out, not_2_out;

  not not_1 (not_1_out, D);
  not not_2 (not_2_out, Clk);
  _2___Clocked_SR_latch_main main_1 (.R(not_1_out), .Clk(not_2_out), .S(D), .Q(Q), .Q_prime(Q_prime));
endmodule

module D_latch_with_EN (
  input  D,
  input  Enable,
  input  Clk,
  output Q,
  output Q_prime
);

  wire and_1_out, not_1_out;

  not not_1 (not_1_out, D);
  and and_1 (and_1_out, Enable, Clk);
  _2___Clocked_SR_latch_main main_1 (.R(not_1_out), .Clk(and_1_out), .S(D), .Q(Q), .Q_prime(Q_prime));
endmodule

module Full_D_latch (
  input  D,
  input  Clear,
  input  Enable,
  input  Clk,
  output Q,
  output Q_prime
);

  wire and_1_out, and_2_out, not_1_out, not_2_out, or_1_out;

  not not_1 (not_1_out, Clear);
  not not_2 (not_2_out, and_1_out);
  and and_1 (and_1_out, D, not_1_out);
  _2___Clocked_SR_latch_main main_1 (.R(not_2_out), .Clk(or_1_out), .S(and_1_out), .Q(Q), .Q_prime(Q_prime));
  or or_1 (or_1_out, Clear, and_2_out);
  and and_2 (and_2_out, Enable, Clk);
endmodule

module Simple_D_flip_flop (
  input  D,
  input  Clk,
  output Q,
  output Q_prime
);

  wire main_1_q, not_1_out;

  main main_1 (.Clk(Clk), .D(D), .Q(main_1_q));  // open: Q_prime
  not not_1 (not_1_out, Clk);
  main main_2 (.Clk(not_1_out), .D(main_1_q), .Q(Q), .Q_prime(Q_prime));

  // Notes on the sheet:
  //   Positive-edge triggered D-flip-flop
endmodule
