// Logisim project 5 - D-type master-slave flip-flop.circ as structural Verilog: 1 circuit, main circuit main
module main (
  input  Clr,
  input  D,
  input  Clk,
  input  En,
  output Q,
  output Q_prime
);

  wire nor_1_out, nor_2_out, nor_3_out, nor_4_out, nor_5_out, nor_6_out, nor_7_out, not_1_out, not_2_out,
       not_3_out, not_4_out, or_1_out, or_2_out;

  not not_1 (not_1_out, Clk);
  not not_2 (not_2_out, En);
  nor nor_1 (nor_1_out, not_1_out, not_2_out);
  not not_3 (not_3_out, D);
  or or_1 (or_1_out, Clr, nor_1_out);
  nor nor_2 (nor_2_out, not_3_out, or_1_out);
  nor nor_3 (nor_3_out, or_1_out, D);
  or or_2 (or_2_out, nor_4_out, Clr);
  nor nor_4 (nor_4_out, nor_2_out, nor_5_out);
  nor nor_5 (nor_5_out, or_2_out, nor_3_out);
  not not_4 (not_4_out, or_1_out);
  nor nor_6 (nor_6_out, nor_5_out, not_4_out);
  nor nor_7 (nor_7_out, nor_4_out, not_4_out);
  nor nor_8 (Q, nor_6_out, Q_prime);
  nor nor_9 (Q_prime, Q, nor_7_out);

  // Notes on the sheet:
  //   Positive edge-triggered D-type master-slave flip-flop
  //   The OR gates used here will need Minecraft Redstone repeaters on some of the inputs to prevent unintended back-flow of power.
endmodule
