// Logisim project 6 - D-type 8-bit register.circ as structural Verilog: 1 circuit, main circuit main
module main (
  input  Clk,
  input  En,
  input  Clr,
  input  [7:0] in_4,
  output [7:0] out_5
);

  _5___D_type_master_slave_flip_flop_main main_1 (
    .Clr(Clr), .D(in_4[0]), .Clk(Clk), .Q(out_5[0]), .En(En));  // open: Q_prime
  _5___D_type_master_slave_flip_flop_main main_2 (
    .Clr(Clr), .D(in_4[1]), .Clk(Clk), .Q(out_5[1]), .En(En));  // open: Q_prime
  _5___D_type_master_slave_flip_flop_main main_3 (
    .Clr(Clr), .D(in_4[2]), .Clk(Clk), .Q(out_5[2]), .En(En));  // open: Q_prime
  _5___D_type_master_slave_flip_flop_main main_4 (
    .Clr(Clr), .D(in_4[3]), .Clk(Clk), .Q(out_5[3]), .En(En));  // open: Q_prime
  _5___D_type_master_slave_flip_flop_main main_5 (
    .Clr(Clr), .D(in_4[4]), .Clk(Clk), .Q(out_5[4]), .En(En));  // open: Q_prime
  _5___D_type_master_slave_flip_flop_main main_6 (
    .Clr(Clr), .D(in_4[5]), .Clk(Clk), .Q(out_5[5]), .En(En));  // open: Q_prime
  _5___D_type_master_slave_flip_flop_main main_7 (
    .Clr(Clr), .D(in_4[6]), .Clk(Clk), .Q(out_5[6]), .En(En));  // open: Q_prime
  _5___D_type_master_slave_flip_flop_main main_8 (
    .Clr(Clr), .D(in_4[7]), .Clk(Clk), .Q(out_5[7]), .En(En));  // open: Q_prime
endmodule
