// Logisim project 7 - Weak pull-down gates.circ as structural Verilog: 1 circuit, main circuit main
module main (
  input  A,
  input  A_2,
  input  B,
  input  A_3,
  input  B_2,
  output Q,
  output Q_2,
  output Q_3
);

  Transistor transistor_1 (.in(1'b1), .out(Q), .gate(A_2));
  Pull_Resistor pull_resistor_1 (.node(Q));
  Transistor #(.\type ("n")) transistor_2 (.in(1'b1), .out(Q_3), .gate(A_3));
  Pull_Resistor pull_resistor_2 (.node(Q_3));
  Pull_Resistor pull_resistor_3 (.node(A));
  Transistor #(.\type ("n")) transistor_3 (.in(1'b1), .out(Q_3), .gate(B_2));

  assign B = A;
  assign Q_2 = A;

  // Notes on the sheet:
  //   Minecraft-style NOT gate
  //   Protected Minecraft-style OR gate
  //   Minecraft-style OR gate
  //   (The transistors can be replaced with diode-like repeaters)
endmodule
