// Logisim project 8 - 4 to 1 MUX.circ as structural Verilog: 3 circuits, main circuit main
module main (
  input  [1:0] Select,
  input  [3:0] Inputs,
  output Output
);

  wire and_1_out, and_2_out, and_3_out, and_4_out, and_5_out, and_6_out, and_7_out, and_8_out, not_1_out,
       not_2_out, or_1_out, or_2_out;

  not not_1 (not_1_out, Select[0]);
  not not_2 (not_2_out, Select[1]);
  and and_1 (and_1_out, not_1_out, not_2_out);
  and and_2 (and_2_out, Select[0], not_2_out);
  and and_3 (and_3_out, not_1_out, Select[1]);
  and and_4 (and_4_out, Select[1], Select[0]);
  and and_5 (and_5_out, Inputs[0], and_1_out);
  and and_6 (and_6_out, and_2_out, Inputs[1]);
  and and_7 (and_7_out, and_3_out, Inputs[2]);
  and and_8 (and_8_out, and_4_out, Inputs[3]);
  or or_1 (or_1_out, and_5_out, and_6_out);
  or or_2 (or_2_out, and_7_out, and_8_out);
  or or_3 (Output, or_1_out, or_2_out);
endmodule

module Expansion_to_NOR (
  input  [1:0] Select,
  input  [3:0] Inputs,
  output Output
);

  wire nor_1_out, nor_2_out, nor_3_out, nor_4_out, nor_5_out, nor_6_out, nor_7_out, nor_8_out, nor_9_out,
       nor_10_out, nor_11_out, not_1_out, not_2_out, not_3_out, not_4_out, not_5_out, not_6_out, not_7_out,
       not_8_out, not_9_out, not_10_out, not_11_out, not_12_out, not_13_out, not_14_out, not_15_out,
       not_16_out, not_17_out, not_18_out, not_19_out, not_20_out;

  not not_1 (not_1_out, Select[0]);
  not not_2 (not_2_out, Select[1]);
  not not_3 (not_3_out, not_1_out);
  not not_4 (not_4_out, not_2_out);
  not not_5 (not_5_out, Select[0]);
  not not_6 (not_6_out, not_2_out);
  not not_7 (not_7_out, not_1_out);
  not not_8 (not_8_out, Select[1]);
  not not_9 (not_9_out, Select[1]);
  not not_10 (not_10_out, Select[0]);
  nor nor_1 (nor_1_out, not_3_out, not_4_out);
  nor nor_2 (nor_2_out, not_5_out, not_6_out);
  nor nor_3 (nor_3_out, not_7_out, not_8_out);
  nor nor_4 (nor_4_out, not_9_out, not_10_out);
  not not_11 (not_11_out, Inputs[0]);
  nor nor_5 (nor_5_out, not_11_out, not_12_out);
  not not_12 (not_12_out, nor_1_out);
  not not_13 (not_13_out, nor_2_out);
  nor nor_6 (nor_6_out, not_13_out, not_14_out);
  not not_14 (not_14_out, Inputs[1]);
  not not_15 (not_15_out, nor_3_out);
  nor nor_7 (nor_7_out, not_15_out, not_16_out);
  not not_16 (not_16_out, Inputs[2]);
  not not_17 (not_17_out, nor_4_out);
  nor nor_8 (nor_8_out, not_17_out, not_18_out);
  not not_18 (not_18_out, Inputs[3]);
  nor nor_9 (nor_9_out, nor_5_out, nor_6_out);
  nor nor_10 (nor_10_out, nor_7_out, nor_8_out);
  not not_19 (not_19_out, nor_9_out);
  nor nor_11 (nor_11_out, not_19_out, not_20_out);
  not not_20 (not_20_out, nor_10_out);
  not not_21 (Output, nor_11_out);
endmodule

module Optimisation (
  input  [1:0] Select,
  input  [3:0] Inputs,
  output Output
);

  wire nor_1_out, nor_2_out, nor_3_out, nor_4_out, not_1_out, not_2_out, not_3_out, not_4_out, not_5_out,
       not_6_out, or_1_out, or_2_out, or_3_out, or_4_out;

  not not_1 (not_1_out, Select[1]);
  not not_2 (not_2_out, Select[0]);
  or or_1 (or_1_out, Select[0], Select[1]);
  or or_2 (or_2_out, not_2_out, Select[1]);
  or or_3 (or_3_out, Select[0], not_1_out);
  or or_4 (or_4_out, not_1_out, not_2_out);
  nor nor_1 (nor_1_out, or_1_out, not_3_out);
  not not_3 (not_3_out, Inputs[0]);
  nor nor_2 (nor_2_out, or_2_out, not_4_out);
  not not_4 (not_4_out, Inputs[1]);
  nor nor_3 (nor_3_out, or_3_out, not_5_out);
  not not_5 (not_5_out, Inputs[2]);
  nor nor_4 (nor_4_out, or_4_out, not_6_out);
  not not_6 (not_6_out, Inputs[3]);
  or or_5 (Output, nor_1_out, nor_2_out, nor_3_out, nor_4_out);

  // Notes on the sheet:
  //   In Minecraft, an 'OR' gate is just connecting two redstone wires together, so that's 'more optimal'
  //   (In technical terms, we might say Redstone wires behave like a 'weak pull down')
endmodule
