// Logisim project X - Adder loop.circ as structural Verilog: 1 circuit, main circuit main
module main (
  input  in_1,
  input  in_2,
  input  Clk,
  input  [7:0] in_4,
  input  in_5
);

  wire [7:0] main_1_out_5, main_2_out;

  // Probe on main_1_out_5
  _6___D_type_8_bit_register_main main_1 (.in_4(main_2_out), .Clk(Clk), .En(in_2), .Clr(in_1), .out_5(main_1_out_5));
  _5___8_bit_Adder_main main_2 (.A(main_1_out_5), .Out(main_2_out), .CIn(in_5), .B(in_4));  // open: COut
endmodule
