// Logisim project Memory Recorded.circ as structural Verilog: 2 circuits, main circuit main
module main (
  input  [7:0] Address,
  input  Write,
  input  Clr,
  input  Clk,
  input  [7:0] Data_In,
  output [7:0] Data_Output
);

  wire or_3_out, or_4_out, or_5_out, or_6_out, or_7_out, or_8_out, or_9_out, or_10_out, or_11_out, or_12_out,
       or_13_out, or_14_out, or_15_out, or_16_out, or_17_out, or_18_out, or_19_out, or_20_out, or_21_out,
       or_22_out, or_23_out, or_24_out, or_25_out, or_26_out, or_27_out, or_28_out, or_29_out, or_30_out,
       or_31_out, or_32_out, or_33_out, or_34_out, or_35_out, or_36_out, or_37_out, or_38_out, or_39_out,
       or_40_out, or_41_out, or_42_out, or_43_out, or_44_out, or_45_out, or_46_out, or_47_out, or_48_out,
       or_49_out, or_50_out, or_51_out, or_52_out, or_53_out, or_54_out, or_55_out, or_56_out, or_57_out,
       or_58_out, or_59_out, or_60_out, or_61_out, or_62_out, or_63_out, or_64_out, or_65_out, or_66_out;
  wire [7:0] buffered_output_2_out_3, buffered_output_3_out_3, decoder_1_out_2, decoder_2_out_2,
       mem_block_1_out_7, mem_block_2_out_7, mem_block_3_out_7, mem_block_4_out_7, mem_block_5_out_7,
       mem_block_6_out_7, mem_block_7_out_7, mem_block_8_out_7, mem_block_9_out_7, mem_block_10_out_7,
       mem_block_11_out_7, mem_block_12_out_7, mem_block_13_out_7, mem_block_14_out_7, mem_block_15_out_7,
       mem_block_16_out_7, mem_block_17_out_7, mem_block_18_out_7, mem_block_19_out_7, mem_block_20_out_7,
       mem_block_21_out_7, mem_block_22_out_7, mem_block_23_out_7, mem_block_24_out_7, mem_block_25_out_7,
       mem_block_26_out_7, mem_block_27_out_7, mem_block_28_out_7, mem_block_29_out_7, mem_block_30_out_7,
       mem_block_31_out_7, mem_block_32_out_7, or_1_out, or_2_out;
  wire [7:7] not_1_out;

  not not_1 (not_1_out[7], Write);
  Decoder decoder_1 (.in_1(Address[2:0]), .out_2(decoder_1_out_2));
  Decoder decoder_2 (.in_1({1'b0, Address[4:3]}), .out_2(decoder_2_out_2));
  assign or_1_out = decoder_1_out_2 | {8{not_1_out[7]}};  // OR_Gate or_1, 8 bits wide
  assign or_2_out = decoder_2_out_2 | {8{not_1_out[7]}};  // OR_Gate or_2, 8 bits wide
  or or_3 (or_3_out, or_2_out[0], or_1_out[7]);
  or or_4 (or_4_out, decoder_2_out_2[0], decoder_1_out_2[7]);
  Mem_Block mem_block_1 (
    .in_5(Data_In), .out_7(mem_block_1_out_7), .R(or_4_out), .W(or_3_out), .Clr(Clr), .Clk(Clk),
    .in_6({8{1'b0}}));
  or or_5 (or_5_out, or_2_out[1], or_1_out[7]);
  or or_6 (or_6_out, decoder_2_out_2[1], decoder_1_out_2[7]);
  Mem_Block mem_block_2 (
    .in_5(Data_In), .out_7(mem_block_2_out_7), .R(or_6_out), .W(or_5_out), .Clr(Clr), .Clk(Clk),
    .in_6({8{1'b0}}));
  or or_7 (or_7_out, decoder_2_out_2[2], decoder_1_out_2[7]);
  or or_8 (or_8_out, or_2_out[2], or_1_out[7]);
  Mem_Block mem_block_3 (
    .in_5(Data_In), .out_7(mem_block_3_out_7), .R(or_7_out), .W(or_8_out), .Clr(Clr), .Clk(Clk),
    .in_6({8{1'b0}}));
  or or_9 (or_9_out, decoder_2_out_2[3], decoder_1_out_2[7]);
  or or_10 (or_10_out, or_2_out[3], or_1_out[7]);
  Mem_Block mem_block_4 (
    .in_5(Data_In), .out_7(mem_block_4_out_7), .R(or_9_out), .W(or_10_out), .Clr(Clr), .Clk(Clk),
    .in_6({8{1'b0}}));
  or or_11 (or_11_out, or_2_out[0], or_1_out[6]);
  or or_12 (or_12_out, decoder_2_out_2[0], decoder_1_out_2[6]);
  Mem_Block mem_block_5 (
    .in_5(Data_In), .out_7(mem_block_5_out_7), .R(or_12_out), .W(or_11_out), .Clr(Clr), .Clk(Clk),
    .in_6(mem_block_1_out_7));
  or or_13 (or_13_out, or_2_out[1], or_1_out[6]);
  or or_14 (or_14_out, decoder_2_out_2[1], decoder_1_out_2[6]);
  Mem_Block mem_block_6 (
    .in_5(Data_In), .out_7(mem_block_6_out_7), .R(or_14_out), .W(or_13_out), .Clr(Clr), .Clk(Clk),
    .in_6(mem_block_2_out_7));
  or or_15 (or_15_out, decoder_2_out_2[2], decoder_1_out_2[6]);
  or or_16 (or_16_out, or_2_out[2], or_1_out[6]);
  Mem_Block mem_block_7 (
    .in_5(Data_In), .out_7(mem_block_7_out_7), .R(or_15_out), .W(or_16_out), .Clr(Clr), .Clk(Clk),
    .in_6(mem_block_3_out_7));
  or or_17 (or_17_out, or_2_out[3], or_1_out[6]);
  or or_18 (or_18_out, decoder_2_out_2[3], decoder_1_out_2[6]);
  Mem_Block mem_block_8 (
    .in_5(Data_In), .out_7(mem_block_8_out_7), .R(or_18_out), .W(or_17_out), .Clr(Clr), .Clk(Clk),
    .in_6(mem_block_4_out_7));
  or or_19 (or_19_out, decoder_2_out_2[0], decoder_1_out_2[5]);
  Mem_Block mem_block_9 (
    .in_5(Data_In), .out_7(mem_block_9_out_7), .R(or_19_out), .W(or_23_out), .Clr(Clr), .Clk(Clk),
    .in_6(mem_block_5_out_7));
  or or_20 (or_20_out, decoder_2_out_2[1], decoder_1_out_2[5]);
  Mem_Block mem_block_10 (
    .in_5(Data_In), .out_7(mem_block_10_out_7), .R(or_20_out), .W(or_24_out), .Clr(Clr), .Clk(Clk),
    .in_6(mem_block_6_out_7));
  or or_21 (or_21_out, decoder_2_out_2[2], decoder_1_out_2[5]);
  Mem_Block mem_block_11 (
    .in_5(Data_In), .out_7(mem_block_11_out_7), .R(or_21_out), .W(or_25_out), .Clr(Clr), .Clk(Clk),
    .in_6(mem_block_7_out_7));
  or or_22 (or_22_out, decoder_2_out_2[3], decoder_1_out_2[5]);
  Mem_Block mem_block_12 (
    .in_5(Data_In), .out_7(mem_block_12_out_7), .R(or_22_out), .W(or_26_out), .Clr(Clr), .Clk(Clk),
    .in_6(mem_block_8_out_7));
  or or_23 (or_23_out, or_2_out[0], or_1_out[5]);
  or or_24 (or_24_out, or_2_out[1], or_1_out[5]);
  or or_25 (or_25_out, or_2_out[2], or_1_out[5]);
  or or_26 (or_26_out, or_2_out[3], or_1_out[5]);
  or or_27 (or_27_out, or_2_out[0], or_1_out[4]);
  or or_28 (or_28_out, decoder_2_out_2[0], decoder_1_out_2[4]);
  Mem_Block mem_block_13 (
    .in_5(Data_In), .out_7(mem_block_13_out_7), .R(or_28_out), .W(or_27_out), .Clr(Clr), .Clk(Clk),
    .in_6(mem_block_9_out_7));
  or or_29 (or_29_out, or_2_out[1], or_1_out[4]);
  or or_30 (or_30_out, decoder_2_out_2[1], decoder_1_out_2[4]);
  Mem_Block mem_block_14 (
    .in_5(Data_In), .out_7(mem_block_14_out_7), .R(or_30_out), .W(or_29_out), .Clr(Clr), .Clk(Clk),
    .in_6(mem_block_10_out_7));
  or or_31 (or_31_out, decoder_2_out_2[2], decoder_1_out_2[4]);
  or or_32 (or_32_out, or_2_out[2], or_1_out[4]);
  Mem_Block mem_block_15 (
    .in_5(Data_In), .out_7(mem_block_15_out_7), .R(or_31_out), .W(or_32_out), .Clr(Clr), .Clk(Clk),
    .in_6(mem_block_11_out_7));
  or or_33 (or_33_out, decoder_2_out_2[3], decoder_1_out_2[4]);
  or or_34 (or_34_out, or_2_out[3], or_1_out[4]);
  Mem_Block mem_block_16 (
    .in_5(Data_In), .out_7(mem_block_16_out_7), .R(or_33_out), .W(or_34_out), .Clr(Clr), .Clk(Clk),
    .in_6(mem_block_12_out_7));
  or or_35 (or_35_out, or_2_out[0], or_1_out[3]);
  or or_36 (or_36_out, decoder_2_out_2[0], decoder_1_out_2[3]);
  Mem_Block mem_block_17 (
    .in_5(Data_In), .out_7(mem_block_17_out_7), .R(or_36_out), .W(or_35_out), .Clr(Clr), .Clk(Clk),
    .in_6(mem_block_13_out_7));
  or or_37 (or_37_out, decoder_2_out_2[1], decoder_1_out_2[3]);
  or or_38 (or_38_out, or_2_out[1], or_1_out[3]);
  Mem_Block mem_block_18 (
    .in_5(Data_In), .out_7(mem_block_18_out_7), .R(or_37_out), .W(or_38_out), .Clr(Clr), .Clk(Clk),
    .in_6(mem_block_14_out_7));
  or or_39 (or_39_out, decoder_2_out_2[2], decoder_1_out_2[3]);
  or or_40 (or_40_out, or_2_out[2], or_1_out[3]);
  Mem_Block mem_block_19 (
    .in_5(Data_In), .out_7(mem_block_19_out_7), .R(or_39_out), .W(or_40_out), .Clr(Clr), .Clk(Clk),
    .in_6(mem_block_15_out_7));
  or or_41 (or_41_out, or_2_out[3], or_1_out[3]);
  or or_42 (or_42_out, decoder_2_out_2[3], decoder_1_out_2[3]);
  Mem_Block mem_block_20 (
    .in_5(Data_In), .out_7(mem_block_20_out_7), .R(or_42_out), .W(or_41_out), .Clr(Clr), .Clk(Clk),
    .in_6(mem_block_16_out_7));
  or or_43 (or_43_out, decoder_2_out_2[0], decoder_1_out_2[2]);
  or or_44 (or_44_out, decoder_2_out_2[1], decoder_1_out_2[2]);
  or or_45 (or_45_out, decoder_2_out_2[2], decoder_1_out_2[2]);
  or or_46 (or_46_out, decoder_2_out_2[3], decoder_1_out_2[2]);
  or or_47 (or_47_out, or_2_out[0], or_1_out[2]);
  Mem_Block mem_block_21 (
    .in_5(Data_In), .out_7(mem_block_21_out_7), .R(or_43_out), .W(or_47_out), .Clr(Clr), .Clk(Clk),
    .in_6(mem_block_17_out_7));
  or or_48 (or_48_out, or_2_out[1], or_1_out[2]);
  Mem_Block mem_block_22 (
    .in_5(Data_In), .out_7(mem_block_22_out_7), .R(or_44_out), .W(or_48_out), .Clr(Clr), .Clk(Clk),
    .in_6(mem_block_18_out_7));
  or or_49 (or_49_out, or_2_out[2], or_1_out[2]);
  Mem_Block mem_block_23 (
    .in_5(Data_In), .out_7(mem_block_23_out_7), .R(or_45_out), .W(or_49_out), .Clr(Clr), .Clk(Clk),
    .in_6(mem_block_19_out_7));
  or or_50 (or_50_out, or_2_out[3], or_1_out[2]);
  Mem_Block mem_block_24 (
    .in_5(Data_In), .out_7(mem_block_24_out_7), .R(or_46_out), .W(or_50_out), .Clr(Clr), .Clk(Clk),
    .in_6(mem_block_20_out_7));
  or or_51 (or_51_out, decoder_2_out_2[0], decoder_1_out_2[1]);
  or or_52 (or_52_out, or_2_out[0], or_1_out[1]);
  Mem_Block mem_block_25 (
    .in_5(Data_In), .out_7(mem_block_25_out_7), .R(or_51_out), .W(or_52_out), .Clr(Clr), .Clk(Clk),
    .in_6(mem_block_21_out_7));
  or or_53 (or_53_out, decoder_2_out_2[1], decoder_1_out_2[1]);
  or or_54 (or_54_out, or_2_out[1], or_1_out[1]);
  Mem_Block mem_block_26 (
    .in_5(Data_In), .out_7(mem_block_26_out_7), .R(or_53_out), .W(or_54_out), .Clr(Clr), .Clk(Clk),
    .in_6(mem_block_22_out_7));
  or or_55 (or_55_out, decoder_2_out_2[2], decoder_1_out_2[1]);
  or or_56 (or_56_out, or_2_out[2], or_1_out[1]);
  Mem_Block mem_block_27 (
    .in_5(Data_In), .out_7(mem_block_27_out_7), .R(or_55_out), .W(or_56_out), .Clr(Clr), .Clk(Clk),
    .in_6(mem_block_23_out_7));
  or or_57 (or_57_out, decoder_2_out_2[3], decoder_1_out_2[1]);
  or or_58 (or_58_out, or_2_out[3], or_1_out[1]);
  Mem_Block mem_block_28 (
    .in_5(Data_In), .out_7(mem_block_28_out_7), .R(or_57_out), .W(or_58_out), .Clr(Clr), .Clk(Clk),
    .in_6(mem_block_24_out_7));
  or or_59 (or_59_out, decoder_2_out_2[0], decoder_1_out_2[0]);
  Mem_Block mem_block_29 (
    .in_5(Data_In), .out_7(mem_block_29_out_7), .R(or_59_out), .W(or_63_out), .Clr(Clr), .Clk(Clk),
    .in_6(mem_block_25_out_7));
  or or_60 (or_60_out, decoder_2_out_2[1], decoder_1_out_2[0]);
  Mem_Block mem_block_30 (
    .in_5(Data_In), .out_7(mem_block_30_out_7), .R(or_60_out), .W(or_64_out), .Clr(Clr), .Clk(Clk),
    .in_6(mem_block_26_out_7));
  or or_61 (or_61_out, decoder_2_out_2[2], decoder_1_out_2[0]);
  Mem_Block mem_block_31 (
    .in_5(Data_In), .out_7(mem_block_31_out_7), .R(or_61_out), .W(or_65_out), .Clr(Clr), .Clk(Clk),
    .in_6(mem_block_27_out_7));
  or or_62 (or_62_out, decoder_2_out_2[3], decoder_1_out_2[0]);
  Mem_Block mem_block_32 (
    .in_5(Data_In), .out_7(mem_block_32_out_7), .R(or_62_out), .W(or_66_out), .Clr(Clr), .Clk(Clk),
    .in_6(mem_block_28_out_7));
  or or_63 (or_63_out, or_2_out[0], or_1_out[0]);
  or or_64 (or_64_out, or_2_out[1], or_1_out[0]);
  or or_65 (or_65_out, or_2_out[2], or_1_out[0]);
  or or_66 (or_66_out, or_2_out[3], or_1_out[0]);
  Buffered_Output buffered_output_1 (.in_1(mem_block_29_out_7), .out_3(Data_Output), .in_2(buffered_output_2_out_3));
  Buffered_Output buffered_output_2 (
    .in_1(mem_block_30_out_7), .out_3(buffered_output_2_out_3), .in_2(buffered_output_3_out_3));
  Buffered_Output buffered_output_3 (
    .in_1(mem_block_31_out_7), .out_3(buffered_output_3_out_3), .in_2(mem_block_32_out_7));
endmodule

module Decoder (
  input  [2:0] in_1,
  output [7:0] out_2
);

  wire not_1_out, not_2_out, not_3_out;

  not not_1 (not_1_out, in_1[0]);
  not not_2 (not_2_out, in_1[1]);
  not not_3 (not_3_out, in_1[2]);
  or or_1 (out_2[0], in_1[0], in_1[1], in_1[2]);
  or or_2 (out_2[1], not_1_out, in_1[1], in_1[2]);
  or or_3 (out_2[2], in_1[0], not_2_out, in_1[2]);
  or or_4 (out_2[3], not_1_out, not_2_out, in_1[2]);
  or or_5 (out_2[4], in_1[0], in_1[1], not_3_out);
  or or_6 (out_2[5], not_1_out, in_1[1], not_3_out);
  or or_7 (out_2[6], in_1[0], not_2_out, not_3_out);
  or or_8 (out_2[7], not_1_out, not_2_out, not_3_out);
endmodule
