// Logisim project Memory.circ as structural Verilog: 6 circuits, main circuit main
module main (
  input  [7:0] Address,
  input  W,
  input  Clr,
  input  Clk,
  input  [7:0] in_5,
  output [7:0] out_6
);

  wire or_3_out, or_4_out, or_5_out, or_6_out, or_7_out, or_8_out, or_9_out, or_10_out, or_11_out, or_12_out,
       or_13_out, or_14_out, or_15_out, or_16_out, or_17_out, or_18_out, or_19_out, or_20_out, or_21_out,
       or_22_out, or_23_out, or_24_out, or_25_out, or_26_out, or_27_out, or_28_out, or_29_out, or_30_out,
       or_31_out, or_32_out, or_33_out, or_34_out, or_35_out, or_36_out, or_37_out, or_38_out, or_39_out,
       or_40_out, or_41_out, or_42_out, or_43_out, or_44_out, or_45_out, or_46_out, or_47_out, or_48_out,
       or_49_out, or_50_out, or_51_out, or_52_out, or_53_out, or_54_out, or_55_out, or_56_out, or_57_out,
       or_58_out, or_59_out, or_60_out, or_61_out, or_62_out, or_63_out, or_64_out, or_65_out, or_66_out;
  wire [7:0] buffered_output_2_out_3, buffered_output_3_out_3, mem_block_1_out_7, mem_block_2_out_7,
       mem_block_3_out_7, mem_block_4_out_7, mem_block_5_out_7, mem_block_6_out_7, mem_block_7_out_7,
       mem_block_8_out_7, mem_block_9_out_7, mem_block_10_out_7, mem_block_11_out_7, mem_block_12_out_7,
       mem_block_13_out_7, mem_block_14_out_7, mem_block_15_out_7, mem_block_16_out_7, mem_block_17_out_7,
       mem_block_18_out_7, mem_block_19_out_7, mem_block_20_out_7, mem_block_21_out_7, mem_block_22_out_7,
       mem_block_23_out_7, mem_block_24_out_7, mem_block_25_out_7, mem_block_26_out_7, mem_block_27_out_7,
       mem_block_28_out_7, mem_block_29_out_7, mem_block_30_out_7, mem_block_31_out_7, mem_block_32_out_7,
       minecraft_decoder_1_out_2, minecraft_decoder_2_out_2, or_1_out, or_2_out;
  wire [7:7] not_1_out;

  assign or_1_out = minecraft_decoder_2_out_2 | {8{not_1_out[7]}};  // OR_Gate or_1, 8 bits wide
  not not_1 (not_1_out[7], W);
  Minecraft_Decoder minecraft_decoder_1 (.in_1(Address[2:0]), .out_2(minecraft_decoder_1_out_2));
  Minecraft_Decoder minecraft_decoder_2 (.in_1({1'b0, Address[4:3]}), .out_2(minecraft_decoder_2_out_2));
  assign or_2_out = minecraft_decoder_1_out_2 | {8{not_1_out[7]}};  // OR_Gate or_2, 8 bits wide
  or or_3 (or_3_out, minecraft_decoder_2_out_2[0], minecraft_decoder_1_out_2[0]);
  or or_4 (or_4_out, or_1_out[0], or_2_out[0]);
  Mem_Block mem_block_1 (
    .in_5(in_5), .out_7(mem_block_1_out_7), .R(or_3_out), .W(or_4_out), .Clr(Clr), .Clk(Clk));  // open: in_6
  or or_5 (or_5_out, minecraft_decoder_2_out_2[1], minecraft_decoder_1_out_2[0]);
  or or_6 (or_6_out, or_1_out[1], or_2_out[0]);
  Mem_Block mem_block_2 (
    .in_5(in_5), .out_7(mem_block_2_out_7), .R(or_5_out), .W(or_6_out), .Clr(Clr), .Clk(Clk));  // open: in_6
  or or_7 (or_7_out, minecraft_decoder_2_out_2[2], minecraft_decoder_1_out_2[0]);
  or or_8 (or_8_out, or_1_out[2], or_2_out[0]);
  Mem_Block mem_block_3 (
    .in_5(in_5), .out_7(mem_block_3_out_7), .R(or_7_out), .W(or_8_out), .Clr(Clr), .Clk(Clk));  // open: in_6
  or or_9 (or_9_out, minecraft_decoder_2_out_2[3], minecraft_decoder_1_out_2[0]);
  or or_10 (or_10_out, or_1_out[3], or_2_out[0]);
  Mem_Block mem_block_4 (
    .in_5(in_5), .out_7(mem_block_4_out_7), .R(or_9_out), .W(or_10_out), .Clr(Clr), .Clk(Clk));  // open: in_6
  or or_11 (or_11_out, minecraft_decoder_2_out_2[0], minecraft_decoder_1_out_2[1]);
  or or_12 (or_12_out, or_1_out[0], or_2_out[1]);
  Mem_Block mem_block_5 (
    .in_5(in_5), .out_7(mem_block_5_out_7), .R(or_11_out), .W(or_12_out), .Clr(Clr), .Clk(Clk),
    .in_6(mem_block_1_out_7));
  or or_13 (or_13_out, minecraft_decoder_2_out_2[1], minecraft_decoder_1_out_2[1]);
  or or_14 (or_14_out, or_1_out[1], or_2_out[1]);
  Mem_Block mem_block_6 (
    .in_5(in_5), .out_7(mem_block_6_out_7), .R(or_13_out), .W(or_14_out), .Clr(Clr), .Clk(Clk),
    .in_6(mem_block_2_out_7));
  or or_15 (or_15_out, minecraft_decoder_2_out_2[2], minecraft_decoder_1_out_2[1]);
  or or_16 (or_16_out, or_1_out[2], or_2_out[1]);
  Mem_Block mem_block_7 (
    .in_5(in_5), .out_7(mem_block_7_out_7), .R(or_15_out), .W(or_16_out), .Clr(Clr), .Clk(Clk),
    .in_6(mem_block_3_out_7));
  or or_17 (or_17_out, minecraft_decoder_2_out_2[3], minecraft_decoder_1_out_2[1]);
  or or_18 (or_18_out, or_1_out[3], or_2_out[1]);
  Mem_Block mem_block_8 (
    .in_5(in_5), .out_7(mem_block_8_out_7), .R(or_17_out), .W(or_18_out), .Clr(Clr), .Clk(Clk),
    .in_6(mem_block_4_out_7));
  or or_19 (or_19_out, minecraft_decoder_2_out_2[0], minecraft_decoder_1_out_2[2]);
  or or_20 (or_20_out, minecraft_decoder_2_out_2[1], minecraft_decoder_1_out_2[2]);
  or or_21 (or_21_out, minecraft_decoder_2_out_2[2], minecraft_decoder_1_out_2[2]);
  or or_22 (or_22_out, minecraft_decoder_2_out_2[3], minecraft_decoder_1_out_2[2]);
  or or_23 (or_23_out, or_1_out[0], or_2_out[2]);
  Mem_Block mem_block_9 (
    .in_5(in_5), .out_7(mem_block_9_out_7), .R(or_19_out), .W(or_23_out), .Clr(Clr), .Clk(Clk),
    .in_6(mem_block_5_out_7));
  or or_24 (or_24_out, or_1_out[1], or_2_out[2]);
  Mem_Block mem_block_10 (
    .in_5(in_5), .out_7(mem_block_10_out_7), .R(or_20_out), .W(or_24_out), .Clr(Clr), .Clk(Clk),
    .in_6(mem_block_6_out_7));
  or or_25 (or_25_out, or_1_out[2], or_2_out[2]);
  Mem_Block mem_block_11 (
    .in_5(in_5), .out_7(mem_block_11_out_7), .R(or_21_out), .W(or_25_out), .Clr(Clr), .Clk(Clk),
    .in_6(mem_block_7_out_7));
  or or_26 (or_26_out, or_1_out[3], or_2_out[2]);
  Mem_Block mem_block_12 (
    .in_5(in_5), .out_7(mem_block_12_out_7), .R(or_22_out), .W(or_26_out), .Clr(Clr), .Clk(Clk),
    .in_6(mem_block_8_out_7));
  or or_27 (or_27_out, minecraft_decoder_2_out_2[0], minecraft_decoder_1_out_2[3]);
  or or_28 (or_28_out, or_1_out[0], or_2_out[3]);
  Mem_Block mem_block_13 (
    .in_5(in_5), .out_7(mem_block_13_out_7), .R(or_27_out), .W(or_28_out), .Clr(Clr), .Clk(Clk),
    .in_6(mem_block_9_out_7));
  or or_29 (or_29_out, minecraft_decoder_2_out_2[1], minecraft_decoder_1_out_2[3]);
  or or_30 (or_30_out, or_1_out[1], or_2_out[3]);
  Mem_Block mem_block_14 (
    .in_5(in_5), .out_7(mem_block_14_out_7), .R(or_29_out), .W(or_30_out), .Clr(Clr), .Clk(Clk),
    .in_6(mem_block_10_out_7));
  or or_31 (or_31_out, minecraft_decoder_2_out_2[2], minecraft_decoder_1_out_2[3]);
  or or_32 (or_32_out, or_1_out[2], or_2_out[3]);
  Mem_Block mem_block_15 (
    .in_5(in_5), .out_7(mem_block_15_out_7), .R(or_31_out), .W(or_32_out), .Clr(Clr), .Clk(Clk),
    .in_6(mem_block_11_out_7));
  or or_33 (or_33_out, minecraft_decoder_2_out_2[3], minecraft_decoder_1_out_2[3]);
  or or_34 (or_34_out, or_1_out[3], or_2_out[3]);
  Mem_Block mem_block_16 (
    .in_5(in_5), .out_7(mem_block_16_out_7), .R(or_33_out), .W(or_34_out), .Clr(Clr), .Clk(Clk),
    .in_6(mem_block_12_out_7));
  or or_35 (or_35_out, minecraft_decoder_2_out_2[0], minecraft_decoder_1_out_2[4]);
  or or_36 (or_36_out, or_1_out[0], or_2_out[4]);
  Mem_Block mem_block_17 (
    .in_5(in_5), .out_7(mem_block_17_out_7), .R(or_35_out), .W(or_36_out), .Clr(Clr), .Clk(Clk),
    .in_6(mem_block_13_out_7));
  or or_37 (or_37_out, minecraft_decoder_2_out_2[1], minecraft_decoder_1_out_2[4]);
  or or_38 (or_38_out, or_1_out[1], or_2_out[4]);
  Mem_Block mem_block_18 (
    .in_5(in_5), .out_7(mem_block_18_out_7), .R(or_37_out), .W(or_38_out), .Clr(Clr), .Clk(Clk),
    .in_6(mem_block_14_out_7));
  or or_39 (or_39_out, minecraft_decoder_2_out_2[2], minecraft_decoder_1_out_2[4]);
  or or_40 (or_40_out, or_1_out[2], or_2_out[4]);
  Mem_Block mem_block_19 (
    .in_5(in_5), .out_7(mem_block_19_out_7), .R(or_39_out), .W(or_40_out), .Clr(Clr), .Clk(Clk),
    .in_6(mem_block_15_out_7));
  or or_41 (or_41_out, minecraft_decoder_2_out_2[3], minecraft_decoder_1_out_2[4]);
  or or_42 (or_42_out, or_1_out[3], or_2_out[4]);
  Mem_Block mem_block_20 (
    .in_5(in_5), .out_7(mem_block_20_out_7), .R(or_41_out), .W(or_42_out), .Clr(Clr), .Clk(Clk),
    .in_6(mem_block_16_out_7));
  or or_43 (or_43_out, minecraft_decoder_2_out_2[0], minecraft_decoder_1_out_2[5]);
  or or_44 (or_44_out, minecraft_decoder_2_out_2[1], minecraft_decoder_1_out_2[5]);
  or or_45 (or_45_out, minecraft_decoder_2_out_2[2], minecraft_decoder_1_out_2[5]);
  or or_46 (or_46_out, minecraft_decoder_2_out_2[3], minecraft_decoder_1_out_2[5]);
  or or_47 (or_47_out, or_1_out[0], or_2_out[5]);
  Mem_Block mem_block_21 (
    .in_5(in_5), .out_7(mem_block_21_out_7), .R(or_43_out), .W(or_47_out), .Clr(Clr), .Clk(Clk),
    .in_6(mem_block_17_out_7));
  or or_48 (or_48_out, or_1_out[1], or_2_out[5]);
  Mem_Block mem_block_22 (
    .in_5(in_5), .out_7(mem_block_22_out_7), .R(or_44_out), .W(or_48_out), .Clr(Clr), .Clk(Clk),
    .in_6(mem_block_18_out_7));
  or or_49 (or_49_out, or_1_out[2], or_2_out[5]);
  Mem_Block mem_block_23 (
    .in_5(in_5), .out_7(mem_block_23_out_7), .R(or_45_out), .W(or_49_out), .Clr(Clr), .Clk(Clk),
    .in_6(mem_block_19_out_7));
  or or_50 (or_50_out, or_1_out[3], or_2_out[5]);
  Mem_Block mem_block_24 (
    .in_5(in_5), .out_7(mem_block_24_out_7), .R(or_46_out), .W(or_50_out), .Clr(Clr), .Clk(Clk),
    .in_6(mem_block_20_out_7));
  or or_51 (or_51_out, minecraft_decoder_2_out_2[0], minecraft_decoder_1_out_2[6]);
  or or_52 (or_52_out, or_1_out[0], or_2_out[6]);
  Mem_Block mem_block_25 (
    .in_5(in_5), .out_7(mem_block_25_out_7), .R(or_51_out), .W(or_52_out), .Clr(Clr), .Clk(Clk),
    .in_6(mem_block_21_out_7));
  or or_53 (or_53_out, minecraft_decoder_2_out_2[1], minecraft_decoder_1_out_2[6]);
  or or_54 (or_54_out, or_1_out[1], or_2_out[6]);
  Mem_Block mem_block_26 (
    .in_5(in_5), .out_7(mem_block_26_out_7), .R(or_53_out), .W(or_54_out), .Clr(Clr), .Clk(Clk),
    .in_6(mem_block_22_out_7));
  or or_55 (or_55_out, minecraft_decoder_2_out_2[2], minecraft_decoder_1_out_2[6]);
  or or_56 (or_56_out, or_1_out[2], or_2_out[6]);
  Mem_Block mem_block_27 (
    .in_5(in_5), .out_7(mem_block_27_out_7), .R(or_55_out), .W(or_56_out), .Clr(Clr), .Clk(Clk),
    .in_6(mem_block_23_out_7));
  or or_57 (or_57_out, minecraft_decoder_2_out_2[3], minecraft_decoder_1_out_2[6]);
  or or_58 (or_58_out, or_1_out[3], or_2_out[6]);
  Mem_Block mem_block_28 (
    .in_5(in_5), .out_7(mem_block_28_out_7), .R(or_57_out), .W(or_58_out), .Clr(Clr), .Clk(Clk),
    .in_6(mem_block_24_out_7));
  or or_59 (or_59_out, minecraft_decoder_2_out_2[0], minecraft_decoder_1_out_2[7]);
  or or_60 (or_60_out, or_1_out[0], or_2_out[7]);
  Mem_Block mem_block_29 (
    .in_5(in_5), .out_7(mem_block_29_out_7), .R(or_59_out), .W(or_60_out), .Clr(Clr), .Clk(Clk),
    .in_6(mem_block_25_out_7));
  or or_61 (or_61_out, minecraft_decoder_2_out_2[1], minecraft_decoder_1_out_2[7]);
  or or_62 (or_62_out, or_1_out[1], or_2_out[7]);
  Mem_Block mem_block_30 (
    .in_5(in_5), .out_7(mem_block_30_out_7), .R(or_61_out), .W(or_62_out), .Clr(Clr), .Clk(Clk),
    .in_6(mem_block_26_out_7));
  or or_63 (or_63_out, minecraft_decoder_2_out_2[2], minecraft_decoder_1_out_2[7]);
  or or_64 (or_64_out, or_1_out[2], or_2_out[7]);
  Mem_Block mem_block_31 (
    .in_5(in_5), .out_7(mem_block_31_out_7), .R(or_63_out), .W(or_64_out), .Clr(Clr), .Clk(Clk),
    .in_6(mem_block_27_out_7));
  or or_65 (or_65_out, minecraft_decoder_2_out_2[3], minecraft_decoder_1_out_2[7]);
  or or_66 (or_66_out, or_1_out[3], or_2_out[7]);
  Mem_Block mem_block_32 (
    .in_5(in_5), .out_7(mem_block_32_out_7), .R(or_65_out), .W(or_66_out), .Clr(Clr), .Clk(Clk),
    .in_6(mem_block_28_out_7));
  Buffered_Output buffered_output_1 (.in_1(mem_block_29_out_7), .out_3(out_6), .in_2(buffered_output_2_out_3));
  Buffered_Output buffered_output_2 (
    .in_1(mem_block_30_out_7), .out_3(buffered_output_2_out_3), .in_2(buffered_output_3_out_3));
  Buffered_Output buffered_output_3 (
    .in_1(mem_block_31_out_7), .out_3(buffered_output_3_out_3), .in_2(mem_block_32_out_7));

  // Notes on the sheet:
  //   2-to-4 decoder
  //   from a 3-to-8 decoder
  //   We optimise the circuit by noticing that MemBlock uses MemCell
  //   and MemCell would otherwise contain inverters on the R/W inputs
  //   and the OR gates in the grid would usually be NOR gates.
  //   The double inversion can be eliminated.
endmodule

module Buffered_Output (
  input  [7:0] in_1,
  input  [7:0] in_2,
  output [7:0] out_3
);

  Transistor #(.\type ("n")) transistor_1 (.in(1'b1), .out(out_3[0]), .gate(in_1[0]));
  Transistor #(.\type ("n")) transistor_2 (.in(1'b1), .out(out_3[1]), .gate(in_1[1]));
  Transistor #(.\type ("n")) transistor_3 (.in(1'b1), .out(out_3[2]), .gate(in_1[2]));
  Pull_Resistor pull_resistor_1 (.node(out_3[2]));
  Pull_Resistor pull_resistor_2 (.node(out_3[0]));
  Pull_Resistor pull_resistor_3 (.node(out_3[1]));
  Transistor #(.\type ("n")) transistor_4 (.in(1'b1), .out(out_3[3]), .gate(in_1[3]));
  Transistor #(.\type ("n")) transistor_5 (.in(1'b1), .out(out_3[4]), .gate(in_1[4]));
  Transistor #(.\type ("n")) transistor_6 (.in(1'b1), .out(out_3[5]), .gate(in_1[5]));
  Pull_Resistor pull_resistor_4 (.node(out_3[3]));
  Pull_Resistor pull_resistor_5 (.node(out_3[5]));
  Pull_Resistor pull_resistor_6 (.node(out_3[4]));
  Transistor #(.\type ("n")) transistor_7 (.in(1'b1), .out(out_3[6]), .gate(in_1[6]));
  Transistor #(.\type ("n")) transistor_8 (.in(1'b1), .out(out_3[7]), .gate(in_1[7]));
  Pull_Resistor pull_resistor_7 (.node(out_3[6]));
  Pull_Resistor pull_resistor_8 (.node(out_3[7]));
  Transistor #(.\type ("n")) transistor_9 (.in(1'b1), .out(out_3[0]), .gate(in_2[0]));
  Transistor #(.\type ("n")) transistor_10 (.in(1'b1), .out(out_3[1]), .gate(in_2[1]));
  Transistor #(.\type ("n")) transistor_11 (.in(1'b1), .out(out_3[2]), .gate(in_2[2]));
  Transistor #(.\type ("n")) transistor_12 (.in(1'b1), .out(out_3[3]), .gate(in_2[3]));
  Transistor #(.\type ("n")) transistor_13 (.in(1'b1), .out(out_3[4]), .gate(in_2[4]));
  Transistor #(.\type ("n")) transistor_14 (.in(1'b1), .out(out_3[5]), .gate(in_2[5]));
  Transistor #(.\type ("n")) transistor_15 (.in(1'b1), .out(out_3[6]), .gate(in_2[6]));
  Transistor #(.\type ("n")) transistor_16 (.in(1'b1), .out(out_3[7]), .gate(in_2[7]));

  // Notes on the sheet:
  //   in_1: pull=down
  //   in_2: pull=down
  //   Inputs pull down so if they are disconnected, they are 0s.
endmodule

module Mem_Cell (
  input  Rd_En,
  input  Clr,
  input  D,
  input  Clk,
  input  Wr_En,
  output Q
);

  wire nor_1_out, nor_2_out, nor_3_out, nor_4_out, nor_5_out, nor_6_out, nor_7_out, nor_8_out, nor_9_out,
       not_1_out, not_2_out, not_3_out, or_1_out, or_2_out, or_3_out, or_4_out;

  not not_1 (not_1_out, Clk);
  nor nor_1 (nor_1_out, not_1_out, Wr_En);
  not not_2 (not_2_out, D);
  or or_1 (or_1_out, Clr, nor_1_out);
  nor nor_2 (nor_2_out, not_2_out, or_1_out);
  nor nor_3 (nor_3_out, or_1_out, D);
  or or_2 (or_2_out, nor_4_out, Clr);
  nor nor_4 (nor_4_out, nor_2_out, nor_5_out);
  nor nor_5 (nor_5_out, or_2_out, nor_3_out);
  not not_3 (not_3_out, or_1_out);
  or or_3 (or_3_out, Clr, not_3_out);
  nor nor_6 (nor_6_out, nor_5_out, or_3_out);
  or or_4 (or_4_out, Clr, nor_9_out);
  nor nor_7 (nor_7_out, nor_4_out, or_3_out);
  nor nor_8 (nor_8_out, nor_6_out, or_4_out);
  nor nor_9 (nor_9_out, nor_8_out, nor_7_out);
  nor nor_10 (Q, Rd_En, nor_9_out);
endmodule

module Mem_Block (
  input  R,
  input  W,
  input  Clr,
  input  Clk,
  input  [7:0] in_5,
  input  [7:0] in_6,
  output [7:0] out_7
);

  wire [7:0] mem_cell_8_q;

  Mem_Cell mem_cell_1 (.Rd_En(R), .Clr(Clr), .D(in_5[7]), .Clk(Clk), .Wr_En(W), .Q(mem_cell_8_q[7]));
  Mem_Cell mem_cell_2 (.Rd_En(R), .Clr(Clr), .D(in_5[6]), .Clk(Clk), .Wr_En(W), .Q(mem_cell_8_q[6]));
  Mem_Cell mem_cell_3 (.Rd_En(R), .Clr(Clr), .D(in_5[5]), .Clk(Clk), .Wr_En(W), .Q(mem_cell_8_q[5]));
  Mem_Cell mem_cell_4 (.Rd_En(R), .Clr(Clr), .D(in_5[4]), .Clk(Clk), .Wr_En(W), .Q(mem_cell_8_q[4]));
  Mem_Cell mem_cell_5 (.Rd_En(R), .Clr(Clr), .D(in_5[3]), .Clk(Clk), .Wr_En(W), .Q(mem_cell_8_q[3]));
  Buffered_Output buffered_output_1 (.in_1(mem_cell_8_q), .out_3(out_7), .in_2(in_6));
  Mem_Cell mem_cell_6 (.Rd_En(R), .Clr(Clr), .D(in_5[2]), .Clk(Clk), .Wr_En(W), .Q(mem_cell_8_q[2]));
  Mem_Cell mem_cell_7 (.Rd_En(R), .Clr(Clr), .D(in_5[1]), .Clk(Clk), .Wr_En(W), .Q(mem_cell_8_q[1]));
  Mem_Cell mem_cell_8 (.Rd_En(R), .Clr(Clr), .D(in_5[0]), .Clk(Clk), .Wr_En(W), .Q(mem_cell_8_q[0]));

  // Notes on the sheet:
  //   out_7: pull=down
endmodule

module Decoder (
  input  [2:0] in_1,
  output [7:0] out_2
);

  wire nor_1_out, nor_2_out, nor_3_out, nor_4_out, nor_5_out, nor_6_out, nor_7_out, nor_8_out, not_1_out,
       not_2_out, not_3_out, not_4_out, not_5_out, not_6_out, not_7_out, not_8_out, not_9_out, not_10_out,
       not_11_out;

  not not_1 (not_1_out, in_1[0]);
  not not_2 (not_2_out, in_1[1]);
  not not_3 (not_3_out, in_1[2]);
  nor nor_1 (nor_1_out, in_1[1], in_1[2]);
  nor nor_2 (nor_2_out, in_1[1], in_1[2]);
  nor nor_3 (nor_3_out, not_2_out, in_1[2]);
  nor nor_4 (nor_4_out, not_2_out, in_1[2]);
  nor nor_5 (nor_5_out, not_3_out, in_1[1]);
  nor nor_6 (nor_6_out, in_1[1], not_3_out);
  nor nor_7 (nor_7_out, not_2_out, not_3_out);
  nor nor_8 (nor_8_out, not_2_out, not_3_out);
  not not_4 (not_4_out, nor_1_out);
  not not_5 (not_5_out, nor_2_out);
  not not_6 (not_6_out, nor_3_out);
  not not_7 (not_7_out, nor_4_out);
  not not_8 (not_8_out, nor_5_out);
  not not_9 (not_9_out, nor_6_out);
  not not_10 (not_10_out, nor_7_out);
  not not_11 (not_11_out, nor_8_out);
  nor nor_9 (out_2[0], in_1[0], not_4_out);
  nor nor_10 (out_2[1], not_1_out, not_5_out);
  nor nor_11 (out_2[2], in_1[0], not_6_out);
  nor nor_12 (out_2[3], not_1_out, not_7_out);
  nor nor_13 (out_2[4], in_1[0], not_8_out);
  nor nor_14 (out_2[5], not_1_out, not_9_out);
  nor nor_15 (out_2[6], in_1[0], not_10_out);
  nor nor_16 (out_2[7], not_1_out, not_11_out);
endmodule

module Minecraft_Decoder (
  input  [2:0] in_1,
  output [7:0] out_2
);

  wire not_1_out, not_2_out, not_3_out;

  not not_1 (not_1_out, in_1[0]);
  not not_2 (not_2_out, in_1[1]);
  not not_3 (not_3_out, in_1[2]);
  or or_1 (out_2[0], in_1[0], in_1[1], in_1[2]);
  or or_2 (out_2[1], not_1_out, in_1[1], in_1[2]);
  or or_3 (out_2[2], in_1[0], not_2_out, in_1[2]);
  or or_4 (out_2[3], not_1_out, not_2_out, in_1[2]);
  or or_5 (out_2[4], in_1[0], in_1[1], not_3_out);
  or or_6 (out_2[5], not_1_out, in_1[1], not_3_out);
  or or_7 (out_2[6], in_1[0], not_2_out, not_3_out);
  or or_8 (out_2[7], not_1_out, not_2_out, not_3_out);

  // Notes on the sheet:
  //   Minecraft can support OR gates with more than 2 inputs
  //   We turn this into an active-low decoder for the sake of the memory usage
endmodule
