// Logisim project Logic unit.circ as structural Verilog: 1 circuit, main circuit main
module main (
  input  [7:0] A,
  output Z,
  output N
);

  wire or_1_out;

  or or_1 (or_1_out, A[0], A[1], A[2], A[3], A[4], A[5], A[6], A[7]);
  not not_1 (Z, or_1_out);

  assign N = A[7];
endmodule
