// Logisim project Clock phases.circ as structural Verilog: 2 circuits, main circuit main
module main (
  input  Clk,
  input  Clr,
  output P1,
  output P2,
  output P2_2
);

  wire nor_1_out, nor_2_out, nor_3_out, nor_4_out, nor_5_out, nor_6_out, nor_7_out, nor_8_out, nor_9_out,
       nor_10_out, nor_11_out, nor_12_out, nor_13_out, nor_14_out, nor_15_out, nor_16_out, nor_17_out,
       nor_18_out, nor_20_out, nor_22_out, nor_24_out, not_1_out, not_2_out, not_3_out, not_4_out, not_5_out,
       not_6_out, not_7_out, or_1_out, or_2_out, or_3_out, or_4_out, or_5_out, or_6_out, or_7_out, or_8_out,
       or_9_out, or_10_out, or_11_out, or_12_out;

  not not_1 (not_1_out, Clk);
  not not_2 (not_2_out, P2_2);
  or or_1 (or_1_out, Clr, not_1_out);
  not not_3 (not_3_out, P1);
  or or_2 (or_2_out, Clr, not_1_out);
  not not_4 (not_4_out, P2);
  or or_3 (or_3_out, Clr, not_1_out);
  nor nor_1 (nor_1_out, not_2_out, or_1_out);
  nor nor_2 (nor_2_out, or_1_out, P2_2);
  not not_5 (not_5_out, or_1_out);
  nor nor_3 (nor_3_out, not_3_out, or_2_out);
  nor nor_4 (nor_4_out, or_2_out, P1);
  not not_6 (not_6_out, or_2_out);
  nor nor_5 (nor_5_out, not_4_out, or_3_out);
  nor nor_6 (nor_6_out, or_3_out, P2);
  not not_7 (not_7_out, or_3_out);
  or or_4 (or_4_out, Clr, nor_10_out);
  nor nor_7 (nor_7_out, nor_3_out, nor_11_out);
  or or_5 (or_5_out, nor_7_out, Clr);
  nor nor_8 (nor_8_out, nor_5_out, nor_12_out);
  or or_6 (or_6_out, nor_8_out, Clr);
  nor nor_9 (nor_9_out, nor_1_out, or_4_out);
  nor nor_10 (nor_10_out, nor_9_out, nor_2_out);
  nor nor_11 (nor_11_out, or_5_out, nor_4_out);
  nor nor_12 (nor_12_out, or_6_out, nor_6_out);
  nor nor_13 (nor_13_out, nor_10_out, or_7_out);
  nor nor_14 (nor_14_out, nor_9_out, or_7_out);
  or or_7 (or_7_out, Clr, not_5_out);
  nor nor_15 (nor_15_out, nor_11_out, or_8_out);
  nor nor_16 (nor_16_out, nor_7_out, or_8_out);
  or or_8 (or_8_out, Clr, not_6_out);
  nor nor_17 (nor_17_out, nor_12_out, or_9_out);
  nor nor_18 (nor_18_out, nor_8_out, or_9_out);
  or or_9 (or_9_out, Clr, not_7_out);
  or or_10 (or_10_out, P1, Clr);
  or or_11 (or_11_out, Clr, nor_22_out);
  or or_12 (or_12_out, Clr, nor_24_out);
  nor nor_19 (P1, nor_13_out, nor_20_out);
  nor nor_20 (nor_20_out, or_10_out, nor_14_out);
  nor nor_21 (P2, nor_15_out, or_11_out);
  nor nor_22 (nor_22_out, P2, nor_16_out);
  nor nor_23 (P2_2, nor_17_out, or_12_out);
  nor nor_24 (nor_24_out, P2_2, nor_18_out);
endmodule

module Partial (
  input  Clk,
  input  Clr,
  output P1,
  output P2,
  output P2_2
);

  wire nor_1_out, nor_2_out, nor_3_out, nor_4_out, nor_5_out, nor_6_out, nor_7_out, nor_8_out, nor_9_out,
       nor_10_out, nor_11_out, nor_12_out, nor_13_out, nor_14_out, nor_15_out, nor_16_out, nor_17_out,
       nor_18_out, nor_20_out, nor_22_out, nor_24_out, not_1_out, not_2_out, not_3_out, not_4_out, not_5_out,
       not_6_out, not_7_out, or_1_out, or_2_out, or_3_out, or_4_out, or_5_out, or_6_out, or_7_out, or_8_out,
       or_9_out, or_10_out, or_11_out, or_12_out;

  not not_1 (not_1_out, Clk);
  not not_2 (not_2_out, P2_2);
  or or_1 (or_1_out, Clr, not_1_out);
  not not_3 (not_3_out, P1);
  or or_2 (or_2_out, Clr, not_1_out);
  not not_4 (not_4_out, P2);
  or or_3 (or_3_out, Clr, not_1_out);
  nor nor_1 (nor_1_out, not_2_out, or_1_out);
  nor nor_2 (nor_2_out, or_1_out, P2_2);
  not not_5 (not_5_out, or_1_out);
  nor nor_3 (nor_3_out, not_3_out, or_2_out);
  nor nor_4 (nor_4_out, or_2_out, P1);
  not not_6 (not_6_out, or_2_out);
  nor nor_5 (nor_5_out, not_4_out, or_3_out);
  nor nor_6 (nor_6_out, or_3_out, P2);
  not not_7 (not_7_out, or_3_out);
  or or_4 (or_4_out, Clr, nor_10_out);
  nor nor_7 (nor_7_out, nor_3_out, nor_11_out);
  or or_5 (or_5_out, nor_7_out, Clr);
  nor nor_8 (nor_8_out, nor_5_out, nor_12_out);
  or or_6 (or_6_out, nor_8_out, Clr);
  nor nor_9 (nor_9_out, nor_1_out, or_4_out);
  nor nor_10 (nor_10_out, nor_9_out, nor_2_out);
  nor nor_11 (nor_11_out, or_5_out, nor_4_out);
  nor nor_12 (nor_12_out, or_6_out, nor_6_out);
  nor nor_13 (nor_13_out, nor_10_out, or_7_out);
  nor nor_14 (nor_14_out, nor_9_out, or_7_out);
  or or_7 (or_7_out, Clr, not_5_out);
  nor nor_15 (nor_15_out, nor_11_out, or_8_out);
  nor nor_16 (nor_16_out, nor_7_out, or_8_out);
  or or_8 (or_8_out, Clr, not_6_out);
  nor nor_17 (nor_17_out, nor_12_out, or_9_out);
  nor nor_18 (nor_18_out, nor_8_out, or_9_out);
  or or_9 (or_9_out, Clr, not_7_out);
  or or_10 (or_10_out, P1, Clr);
  or or_11 (or_11_out, Clr, nor_22_out);
  or or_12 (or_12_out, Clr, nor_24_out);
  nor nor_19 (P1, nor_13_out, nor_20_out);
  nor nor_20 (nor_20_out, or_10_out, nor_14_out);
  nor nor_21 (P2, nor_15_out, or_11_out);
  nor nor_22 (nor_22_out, P2, nor_16_out);
  nor nor_23 (P2_2, nor_17_out, or_12_out);
  nor nor_24 (nor_24_out, P2_2, nor_18_out);
endmodule
