// Logisim project Decoder.circ as structural Verilog: 1 circuit, main circuit main
module main (
  input  [3:0] Opcode,
  output [15:0] Q
);

  wire not_1_out, not_2_out, not_3_out, not_4_out;

  not not_1 (not_1_out, Opcode[0]);
  not not_2 (not_2_out, Opcode[1]);
  not not_3 (not_3_out, Opcode[2]);
  not not_4 (not_4_out, Opcode[3]);
  nor nor_1 (Q[0], Opcode[0], Opcode[1], Opcode[2], Opcode[3]);
  nor nor_2 (Q[1], not_1_out, Opcode[1], Opcode[2], Opcode[3]);
  nor nor_3 (Q[2], Opcode[0], not_2_out, Opcode[2], Opcode[3]);
  nor nor_4 (Q[3], not_1_out, not_2_out, Opcode[3], Opcode[2]);
  nor nor_5 (Q[4], Opcode[0], Opcode[1], Opcode[3], not_3_out);
  nor nor_6 (Q[5], not_1_out, Opcode[1], not_3_out, Opcode[3]);
  nor nor_7 (Q[6], Opcode[0], not_2_out, not_3_out, Opcode[3]);
  nor nor_8 (Q[7], not_1_out, not_2_out, not_3_out, Opcode[3]);
  nor nor_9 (Q[8], Opcode[0], Opcode[1], Opcode[2], not_4_out);
  nor nor_10 (Q[9], not_1_out, Opcode[1], Opcode[2], not_4_out);
  nor nor_11 (Q[10], Opcode[0], not_2_out, Opcode[2], not_4_out);
  nor nor_12 (Q[11], not_1_out, not_2_out, Opcode[2], not_4_out);
  nor nor_13 (Q[12], Opcode[0], Opcode[1], not_3_out, not_4_out);
  nor nor_14 (Q[13], not_1_out, Opcode[1], not_3_out, not_4_out);
  nor nor_15 (Q[14], Opcode[0], not_2_out, not_3_out, not_4_out);
  nor nor_16 (Q[15], not_1_out, not_2_out, not_3_out, not_4_out);
endmodule
